# Fritzing sketch dht22 (saved by Fritzing 0.9.3b)
breadboards: 2

parts:
  Mod1 = Raspberry Pi Pico
  U1 = LCD-16X2 [package=lcd-16x2_noholes]
  R1 = Resistor [tolerance=±5% resistance=10 package="0805 [SMD]"]
  R2 = Resistor [tolerance=±5% resistance=1k package="0805 [SMD]"]
  R3 = Resistor [tolerance=±5% resistance=2.2k package="0805 [SMD]"]
  R4 = Resistor [tolerance=±5% resistance=1k package="0805 [SMD]"]
  DHT1 = DHT22 Humidity and Temperature Sensor
  Part1 = Bluetooth HC-05 Macho  # not connected

nets:
  N1: Mod1.pin_3, Mod1.pin_8, Mod1.pin_13, Mod1.pin_18, Mod1.pin_23, Mod1.pin_28, Mod1.pin_33, Mod1.pin_38
  N2: Mod1.pin_9, DHT1.DATA
  N3: Mod1.pin_10, U1.E
  N4: Mod1.pin_11, U1.R_W
  N5: Mod1.pin_12, U1.DB0
  N6: Mod1.pin_14, U1.DB1
  N7: Mod1.pin_15, U1.DB2
  N8: Mod1.pin_16, U1.DB3
  N9: Mod1.pin_17, U1.DB4
  N10: Mod1.pin_19, U1.DB5
  N11: Mod1.pin_20, U1.DB6
  N12: Mod1.pin_21, R3.Pin_0, R4.Pin_0
  N13: Mod1.pin_22, U1.RS
  VSS: U1.VSS, R1.Pin_1, R2.Pin_1, DHT1.GND
  VDD: U1.VDD, U1.K, DHT1.VDD
  N14: U1.VO, R2.Pin_0
  N15: U1.DB7, R4.Pin_1
  N16: U1.A, R1.Pin_0

custom parts:
  Raspberry Pi Pico: Raspberry Pi Pico. Based around the RP2040 microcontroller the Pico is a low cost microcontroller device bringing Raspberry Pi quality, cost, and easy of use to the microcontroller space. Jan 2021, Split part in to two versions: tht (this one) and SMD. This one will drill holes for a .1 in header in pcb to allow plugging in the module as well as providing pads to solder the module to the top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
